# Fritzing sketch Mega 2560 mit Ampel und CO2 Sensor (saved by Fritzing 1.0.2b)
breadboards: 1

parts:
  Bauteil2 = Arduino Mega 2560 (Rev3)
  MH-Z19C1 = MH-Z19C
  A1 = BBAA100043

nets:
  N1: Bauteil2.D11_PWM, MH-Z19C1.Rx
  N2: Bauteil2.D10_PWM, MH-Z19C1.Tx
  5V: Bauteil2.5V, MH-Z19C1.Vin
  GND: Bauteil2.GND, MH-Z19C1.GND, A1.pin4
  N3: Bauteil2.D5_PWM, A1.pin3
  N4: Bauteil2.D6_PWM, A1.pin2
  N5: Bauteil2.D7_PWM, A1.pin1

custom parts:
  MH-Z19C: CO2-Sensor https://www.winsen-sensor.com/
  BBAA100043: BBAA100043 traffic light module.
